# Fritzing sketch Electric shema (saved by Fritzing 0.9.3b)
breadboards: 1

parts:
  Part1 = Arduino Uno (Rev3)
  DHT1 = DHT22 Humidity and Temperature Sensor
  R1 = Resistor [tolerance=±5% resistance=220 package="0805 [SMD]"]
  S1 = Momentary Switch [package=ksa_sealed_tac_switch]
  S2 = Momentary Switch [package=ksa_sealed_tac_switch]
  S3 = Momentary Switch [package=ksa_sealed_tac_switch]
  S4 = Momentary Switch [package=ksa_sealed_tac_switch]
  S5 = Momentary Switch [package=ksa_sealed_tac_switch]
  R2 = Resistor [tolerance=±5% resistance=220 package="0805 [SMD]"]
  R3 = Resistor [tolerance=±5% resistance=220 package="0805 [SMD]"]
  R4 = Resistor [tolerance=±5% resistance=220 package="0805 [SMD]"]
  R5 = Resistor [tolerance=±5% resistance=220 package="0805 [SMD]"]
  R6 = Resistor [tolerance=±5% resistance=220 package="0805 [SMD]"]

nets:
  N1: Part1.D2, DHT1.DATA, R1.Pin_0
  N2: Part1.D3_PWM, S5.1
  N3: Part1.D4, S4.1
  N4: Part1.D5_PWM, S3.1
  N5: Part1.D6_PWM, S2.1
  N6: Part1.D7, S1.1
  5V: Part1.5V, DHT1.VDD, R1.Pin_1, S1.4, S2.4, S3.4, S4.4, S5.4
  GND: Part1.GND, DHT1.GND, R2.Pin_0, R3.Pin_1, R4.Pin_1, R5.Pin_1, R6.Pin_1
  N7: S1.2, R2.Pin_1
  N8: S2.2, R3.Pin_0
  N9: S3.2, R4.Pin_0
  N10: S4.2, R5.Pin_0
  N11: S5.2, R6.Pin_0
